# Fritzing sketch buttons (saved by Fritzing 0.9.3b)
breadboards: 1

parts:
  Raspberry_Pi1 = Raspberry Pi Zero
  S1 = Round Pushbutton
  S2 = Round Pushbutton
  S4 = Momentary Switch [package=ksa_sealed_tac_switch]

nets:
  N1: Raspberry_Pi1.GIPO4, S2.leg0
  N2: Raspberry_Pi1.GIPO22, S4.1, S4.2
  N3: Raspberry_Pi1.GIPO23, S1.leg1
  N4: Raspberry_Pi1.GND, S1.leg0, S2.leg1, S4.3, S4.4

custom parts:
  Raspberry Pi Zero: The Raspberry Pi Zero is the latest single board computer to be released by the Raspberry Pi Foundation. It is the entry level model Raspberry Pi perfect for hobbyists, makers and industrial engineers looking to create solutions where small size and low power consumption are important. This is especially relevant for applications in the wearables space as well as up and coming applications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
