# Fritzing sketch leds (saved by Fritzing 0.9.3b)
breadboards: 1

parts:
  Raspberry_Pi1 = Raspberry Pi Zero
  U1 = TRANSISTOR_NPN_2 [package=to-92]
  R1 = Resistor [tolerance=±5% resistance=1k package=THT]
  LED1 = LED - 3mm [color="Red (633nm)" package="3 mm [THT]"]
  LED2 = LED - 3mm [color="Red (633nm)" package="3 mm [THT]"]
  LED3 = LED - 3mm [color="Red (633nm)" package="3 mm [THT]"]
  R2 = Resistor [tolerance=±5% resistance=100 package=THT]
  R3 = Resistor [tolerance=±5% resistance=100 package=THT]
  R4 = Resistor [tolerance=±5% resistance=100 package=THT]

nets:
  N1: Raspberry_Pi1.GIPO25, R1.Pin_0
  N2: Raspberry_Pi1.GND, U1.E
  N3: Raspberry_Pi1.5V, R2.Pin_1, R3.Pin_1, R4.Pin_1
  N4: U1.C, LED1.cathode, LED2.cathode, LED3.cathode
  N5: U1.B, R1.Pin_1
  N6: LED1.anode, R3.Pin_0
  N7: LED2.anode, R2.Pin_0
  N8: LED3.anode, R4.Pin_0

notes:
  100 Ω
  1k Ω

custom parts:
  Raspberry Pi Zero: The Raspberry Pi Zero is the latest single board computer to be released by the Raspberry Pi Foundation. It is the entry level model Raspberry Pi perfect for hobbyists, makers and industrial engineers looking to create solutions where small size and low power consumption are important. This is especially relevant for applications in the wearables space as well as up and coming applications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
