# Fritzing sketch schemaLcd (saved by Fritzing 0.9.3b)
breadboards: 1

parts:
  Raspberry_Pi1 = Raspberry Pi Zero
  U1 = LCD-16X2 [package=lcd-16x2]
  R1 = Rotary Potentiometer (Small) [maximum_resistance=100kΩ package=THT]
  R2 = Resistor [tolerance=±5% resistance=1k package=THT]
  R3 = Resistor [tolerance=±5% resistance=220 package=THT]
  R4 = Resistor [tolerance=±5% resistance=1k package=THT]

nets:
  N1: Raspberry_Pi1.GIPO11, U1.DB7
  N2: Raspberry_Pi1.GIPO5, U1.DB6
  N3: Raspberry_Pi1.GIPO6, U1.DB5
  N4: Raspberry_Pi1.GIPO13, U1.DB4
  N5: Raspberry_Pi1.GIPO19, U1.E
  N6: Raspberry_Pi1.GIPO26, U1.RS
  GND: Raspberry_Pi1.GND, U1.VSS, U1.R_W, R1.leg1, R3.Pin_1
  N7: Raspberry_Pi1.5V, R2.Pin_0, R4.Pin_0
  N8: U1.VO, R1.wiper
  N9: U1.A, R2.Pin_1
  N10: U1.K, R3.Pin_0
  N11: R1.leg2, R4.Pin_1

notes:
  220 Ω
  220Ω
  1k Ω

custom parts:
  Raspberry Pi Zero: The Raspberry Pi Zero is the latest single board computer to be released by the Raspberry Pi Foundation. It is the entry level model Raspberry Pi perfect for hobbyists, makers and industrial engineers looking to create solutions where small size and low power consumption are important. This is especially relevant for applications in the wearables space as well as up and coming applications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
