# Fritzing sketch vibratorMotor (saved by Fritzing 0.9.3b)
breadboards: 1

parts:
  Raspberry_Pi1 = Raspberry Pi Zero
  MOTOR1 = Vibration Motor
  BAT1 = BC9VPC [package=bc9vpc]
  D1 = Schottky Diode [part_number=1N5817 package="Melf DO-213 AB [SMD]"]
  Q1 = NPN-Transistor [package="SOT-23 [SMD]"]
  R1 = Resistor [tolerance=±5% resistance=330 package=THT]

nets:
  N1: Raspberry_Pi1.GIPO27, R1.Pin_0
  N2: Raspberry_Pi1.GND, BAT1.V-, Q1.1
  N3: MOTOR1.POS, BAT1.V+, D1.cathode
  N4: MOTOR1.NEG, D1.anode, Q1.2
  N5: Q1.0, R1.Pin_1

notes:
  330 Ω

custom parts:
  Raspberry Pi Zero: The Raspberry Pi Zero is the latest single board computer to be released by the Raspberry Pi Foundation. It is the entry level model Raspberry Pi perfect for hobbyists, makers and industrial engineers looking to create solutions where small size and low power consumption are important. This is especially relevant for applications in the wearables space as well as up and coming applications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
  Vibration Motor: An eccentric vibration motor!
